# Fritzing sketch scheme (saved by Fritzing 0.9.4)

parts:
  WeMos_D1_Mini_Lite1 = WeMos D1 Mini
  MP3-1 = Serial MP3 Player
  MP3-2 = Serial MP3 Player
  M1 = PAM8403 Stereo Amplifier [part_number=HW-104]
  SP1 = SPEAKER [package=pcb_mount_speaker]
  Компонент1 = InvenSense MPU6050
  NEOPIXEL1 = Neopixel Strip -- Black (30/m)
  NEOPIXEL2 = Neopixel Strip -- Black (30/m)
  BAT1 = 18650 battery holder [package=battery-18650-kit]
  BAT2 = 18650 battery holder [package=battery-18650-kit]
  U1 = LM2596 step down module
  R1 = Resistor [tolerance=±5% resistance=220 package=THT]
  S1 = Pushbutton [package="[THT]"]  # not connected
  S2 = Pushbutton [package="[THT]"]
  R2 = Resistor [tolerance=±5% resistance=220 package=THT]
  S3 = Round Pushbutton
  J2 = Power Jack [package=power_jack_pth]
  C1 = Electrolytic Capacitor [capacitance=1µF package="100 mil [THT, electrolytic]"]

nets:
  3V3: WeMos_D1_Mini_Lite1.3V3, Компонент1.VCC
  N1: WeMos_D1_Mini_Lite1.A0, R1.Pin_0
  N2: WeMos_D1_Mini_Lite1.D0, R2.Pin_1
  N3: WeMos_D1_Mini_Lite1.D1, MP3-2.pin3
  N4: WeMos_D1_Mini_Lite1.D2, MP3-2.pin4
  N5: WeMos_D1_Mini_Lite1.D3, MP3-1.pin3
  N6: WeMos_D1_Mini_Lite1.D4, MP3-1.pin4
  N7: WeMos_D1_Mini_Lite1.D5, S2.Pin_3
  N8: WeMos_D1_Mini_Lite1.D6, Компонент1.SDA
  N9: WeMos_D1_Mini_Lite1.D7, Компонент1.SCL
  N10: WeMos_D1_Mini_Lite1.D8, NEOPIXEL2.Din
  N11: M1.LOUT+, SP1.-
  N12: M1.LOUT-, SP1.+
  N13: M1.POWER-, NEOPIXEL1.GND, BAT2.-, U1.IN-, U1.OUT-, J2.PWR, C1.+
  N14: M1.POWER+, NEOPIXEL1.+5V, U1.OUT+, R2.Pin_0, C1.-
  N15: BAT1.+, S3.leg0, J2.GND
  N16: BAT1.-, BAT2.+
  N17: U1.IN+, R1.Pin_1, S3.leg1

custom parts:
  Serial MP3 Player: The module is a kind of simple MP3 player device which is based on a high-quality MP3 audio chip---YX5300. It can support 8k Hz ~ 48k Hz sampling frequency MP3 and WAV file formats. There is a TF card socket on board, so you can plug the micro SD card that stores audio files. MCU can control the MP3 playback state by sending commands to the module via UART port, such as switch songs, change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
  PAM8403 Stereo Amplifier: PAM8403 stereo amplifier module Descriptive words Links: PAM8403 product datasheet
  Neopixel Strip -- Black (30/m): These NeoPixel strips have 30 digitally-addressable pixel LEDs per meter and are very affordable and are only 12.5 mm wide, 10 mm if you remove the strip from the casing.
  18650 battery holder: 18650 Battery Holder
  LM2596 step down module: LM2596 DC-DC step down power supply module 3 A.
  Round Pushbutton: A generic pushbutton.
  Power Jack: Power Jack This is the standard 5.5mm barrel jack for power. The PTH is the most common, proven, reliable, footprint. All others are experimental. The Slot footprint only works if the mill layer is transmitted to the PCB fab house so be warned. Spark Fun Electronics SKU : PRT-00119. Mating wall wart : TOL-00298 (and others)
